// Logisim project L10Q1_D.circ as structural Verilog: 1 circuit, main circuit main
module main (
  input  c0,
  input  c1,
  output out_3,
  output out_4
);

  wire and_1_out, and_2_out, and_3_out, and_4_out, and_5_out, and_6_out, and_7_out, and_8_out, clock_1_out,
       minus_c0, minus_c1, minus_s0, minus_s1, or_1_out, or_2_out;

  not not_1 (minus_c0, c0);
  not not_2 (minus_c1, c1);
  and and_1 (and_1_out, c0, minus_s0, minus_s1);
  and and_2 (and_2_out, c1, out_4, minus_s1);
  and and_3 (and_3_out, minus_c1, out_4, out_3);
  and and_4 (and_4_out, minus_c0, minus_s0, out_3);
  Clock clock_1 (.out(clock_1_out));
  or or_1 (or_1_out, and_1_out, and_2_out, and_3_out, and_4_out);
  D_Flip_Flop d_ff_1 (.clk(clock_1_out), .D(or_2_out), .Q(out_4), .Qn(minus_s0));  // open: preset, en, reset
  and and_5 (and_5_out, out_4, minus_c0, minus_c1);
  and and_6 (and_6_out, out_4, c1, c0);
  and and_7 (and_7_out, minus_s0, c1, minus_c0);
  and and_8 (and_8_out, minus_s0, minus_c1, c0);
  D_Flip_Flop d_ff_2 (.clk(clock_1_out), .D(or_1_out), .Q(out_3), .Qn(minus_s1));  // open: preset, en, reset
  or or_2 (or_2_out, and_5_out, and_6_out, and_7_out, and_8_out);

  // Other names for the same wires on the sheet: s0 = out_4; s1 = out_3
endmodule
