// Logisim project L10Q1_JK.circ as structural Verilog: 1 circuit, main circuit main
module main (
  input  c0,
  input  c1,
  output q1,
  output q0
);

  wire and_1_out, and_2_out, clock_1_out, not_1_out, or_1_out, xor_1_out;

  not not_1 (not_1_out, q0);
  xor xor_1 (xor_1_out, c0, c1);
  and and_1 (and_1_out, c0, not_1_out);
  and and_2 (and_2_out, c1, q0);
  or or_1 (or_1_out, and_1_out, and_2_out);
  Clock clock_1 (.out(clock_1_out));
  J_K_Flip_Flop j_k_ff_1 (.J(xor_1_out), .clk(clock_1_out), .K(xor_1_out), .Q(q0));  // open: Qn, preset, en, reset
  J_K_Flip_Flop j_k_ff_2 (.J(or_1_out), .clk(clock_1_out), .K(or_1_out), .Q(q1));  // open: Qn, preset, en, reset
endmodule
