// Logisim project L10Q1_SR.circ as structural Verilog: 1 circuit, main circuit main
module main (
  input  c0,
  input  c1,
  output out_3,
  output out_4
);

  wire and_1_out, and_2_out, and_3_out, and_4_out, and_5_out, and_6_out, clock_1_out, not_1_out, not_2_out,
       not_3_out, not_4_out, not_5_out, or_1_out, or_2_out, xor_1_out;

  xor xor_1 (xor_1_out, c1, c0);
  and and_1 (and_1_out, xor_1_out, out_4);
  and and_2 (and_2_out, xor_1_out, not_1_out);
  not not_1 (not_1_out, out_4);
  Clock clock_1 (.out(clock_1_out));
  S_R_Flip_Flop s_r_ff_1 (.S(and_2_out), .clk(clock_1_out), .R(and_1_out), .Q(out_4));  // open: Qn, preset, reset, en
  not not_2 (not_2_out, out_3);
  not not_3 (not_3_out, out_4);
  not not_4 (not_4_out, out_3);
  and and_3 (and_3_out, c0, not_2_out, not_3_out);
  and and_4 (and_4_out, c1, not_4_out, out_4);
  S_R_Flip_Flop s_r_ff_2 (.S(or_1_out), .clk(clock_1_out), .R(or_2_out), .Q(out_3));  // open: Qn, preset, reset, en
  or or_1 (or_1_out, and_3_out, and_4_out);
  not not_5 (not_5_out, out_4);
  and and_5 (and_5_out, c1, out_3, out_4);
  and and_6 (and_6_out, c0, out_3, not_5_out);
  or or_2 (or_2_out, and_5_out, and_6_out);

  // Other names for the same wires on the sheet: q0 = out_4; q1 = out_3
endmodule
