// Logisim project L10Q1_T.circ as structural Verilog: 1 circuit, main circuit main
module main (
  input  c0,
  input  c1,
  output q1,
  output q0
);

  wire and_1_out, and_2_out, clock_1_out, not_1_out, or_1_out, xor_1_out;

  not not_1 (not_1_out, q0);
  and and_1 (and_1_out, not_1_out, c0);
  or or_1 (or_1_out, and_1_out, and_2_out);
  and and_2 (and_2_out, c1, q0);
  xor xor_1 (xor_1_out, c0, c1);
  Clock clock_1 (.out(clock_1_out));
  T_Flip_Flop t_ff_1 (.clk(clock_1_out), .T(xor_1_out), .Q(q0));  // open: Qn, preset, reset, en
  T_Flip_Flop t_ff_2 (.clk(clock_1_out), .T(or_1_out), .Q(q1));  // open: Qn, preset, reset, en
endmodule
