// Logisim project L10Q2.circ as structural Verilog: 1 circuit, main circuit main
module main (
  input  reset,
  output [8:0] out_2
);

  wire adder_1_cout, adder_1_out, clock_1_out, shift_register_1_out, shift_register_2_out;

  Clock clock_1 (.out(clock_1_out));
  Shift_Register shift_register_1 (
    .in(shift_register_1_out), .clk(clock_1_out), .out(shift_register_1_out), .clr(reset));  // open: shift, load, d0, q0, d1, q1, d2, q2, d3, q3, d4, q4, d5, q5, d6, q6, d7, q7
  Shift_Register shift_register_2 (
    .in(shift_register_2_out), .clk(clock_1_out), .out(shift_register_2_out), .clr(reset));  // open: shift, load, d0, q0, d1, q1, d2, q2, d3, q3, d4, q4, d5, q5, d6, q6, d7, q7
  Adder #(.width(1)) adder_1 (
    .a(shift_register_1_out), .b(shift_register_2_out), .out(adder_1_out), .cin(out_2[8]), .cout(adder_1_cout));
  Register #(.width(1)) register_1 (.D(adder_1_cout), .Q(out_2[8]), .clk(clock_1_out), .clr(reset));  // open: en
  Shift_Register shift_register_3 (
    .in(adder_1_out), .clk(clock_1_out), .clr(reset), .q0(out_2[7]), .q1(out_2[6]), .q2(out_2[5]),
    .q3(out_2[4]), .q4(out_2[3]), .q5(out_2[2]), .q6(out_2[1]), .q7(out_2[0]));  // open: shift, out, load, d0, d1, d2, d3, d4, d5, d6, d7
endmodule
