// Logisim project L10Q3.circ as structural Verilog: 2 circuits, main circuit main
module main (
);

  wire c0, c1, clock_1_out, nor_1_out;
  wire [3:2] n2_bit_counter_1_c0;

  nor nor_1 (nor_1_out, c0, c1);
  _2_bit_counter u_2_bit_counter_1 (.clk(nor_1_out), .c0(n2_bit_counter_1_c0[2]), .c1(n2_bit_counter_1_c0[3]));
  Hex_Digit_Display hex_digit_display_1 (.value({n2_bit_counter_1_c0, c1, c0}));  // open: dp
  Clock clock_1 (.out(clock_1_out));
  _2_bit_counter u_2_bit_counter_2 (.clk(clock_1_out), .c0(c0), .c1(c1));
endmodule

module _2_bit_counter (
  input  clk,
  output c0,
  output c1
);

  wire xor_1_out, xor_2_out;

  xor xor_1 (xor_1_out, 1'b1, c0);
  D_Flip_Flop d_ff_1 (.clk(clk), .D(xor_1_out), .Q(c0));  // open: Qn, preset, en, reset
  D_Flip_Flop d_ff_2 (.clk(clk), .D(xor_2_out), .Q(c1));  // open: Qn, preset, en, reset
  xor xor_2 (xor_2_out, c0, c1);
endmodule
