// Logisim project L11Q2_J-K-mealy.circ as structural Verilog: 1 circuit, main circuit main
module main (
  input  \input ,
  input  clear,
  output out_3,
  output out_4,
  output \output 
);

  wire and_1_out, clk_out, not_1_out, not_2_out, or_1_out, xor_1_out;

  not not_1 (not_1_out, \input );
  not not_2 (not_2_out, out_3);
  and and_1 (and_1_out, \input , out_4);
  xor xor_1 (xor_1_out, out_3, \input );
  or or_1 (or_1_out, not_1_out, not_2_out);
  Clock clk (.out(clk_out));
  J_K_Flip_Flop j_k_ff_1 (.J(and_1_out), .clk(clk_out), .K(out_4), .Q(out_3), .reset(clear));  // open: Qn, preset, en
  J_K_Flip_Flop j_k_ff_2 (
    .J(xor_1_out), .clk(clk_out), .K(or_1_out), .Q(out_4), .reset(clear));  // open: Qn, preset, en
  and and_2 (\output , out_3, out_4, \input );

  // Other names for the same wires on the sheet: C0 = out_4; C1 = out_3; I0 = \input 
endmodule
