// Logisim project L11Q2_J-K-moore.circ as structural Verilog: 1 circuit, main circuit main
module main (
  input  \input ,
  input  reset,
  output \output 
);

  wire and_1_out, and_2_out, and_3_out, and_4_out, and_5_out, C0, C1, Clock_out, not_1_out, not_2_out,
       not_3_out, or_1_out, or_2_out;

  not not_1 (not_1_out, \output );
  and and_1 (and_1_out, \output , \input );
  or or_1 (or_1_out, and_1_out, and_2_out);
  and and_2 (and_2_out, C0, \input );
  not not_2 (not_2_out, \input );
  and and_3 (and_3_out, not_2_out, C1);
  not not_3 (not_3_out, C1);
  and and_4 (and_4_out, not_3_out, not_1_out, \input );
  Clock Clock (.out(Clock_out));
  and and_5 (and_5_out, \input , C1, C0);
  or or_2 (or_2_out, and_3_out, and_4_out);
  J_K_Flip_Flop j_k_ff_1 (
    .J(and_5_out), .clk(Clock_out), .K(1'b1), .Q(\output ), .reset(reset));  // open: Qn, preset, en
  J_K_Flip_Flop j_k_ff_2 (.J(or_1_out), .clk(Clock_out), .K(C0), .Q(C1), .reset(reset));  // open: Qn, preset, en
  J_K_Flip_Flop j_k_ff_3 (.J(or_2_out), .clk(Clock_out), .K(1'b1), .Q(C0), .reset(reset));  // open: Qn, preset, en

  // Other names for the same wires on the sheet: C2 = \output ; I0 = \input 
endmodule
