// Logisim project L11Q2_T-mealy.circ as structural Verilog: 1 circuit, main circuit main
module main (
  input  \input ,
  input  in_2,
  output \output 
);

  wire and_1_out, and_2_out, and_3_out, C0, C1, clk_out, not_1_out, or_1_out, or_2_out, xor_1_out;

  not not_1 (not_1_out, C1);
  and and_1 (and_1_out, \input , C0);
  or or_1 (or_1_out, and_1_out, and_2_out);
  and and_2 (and_2_out, C1, C0);
  xor xor_1 (xor_1_out, C1, \input );
  and and_3 (and_3_out, C0, not_1_out);
  Clock clk (.out(clk_out));
  or or_2 (or_2_out, xor_1_out, and_3_out);
  T_Flip_Flop t_ff_1 (.clk(clk_out), .T(or_1_out), .Q(C1), .reset(in_2));  // open: Qn, preset, en
  T_Flip_Flop t_ff_2 (.clk(clk_out), .T(or_2_out), .Q(C0), .reset(in_2));  // open: Qn, preset, en
  and and_4 (\output , C1, C0, \input );

  // Other names for the same wires on the sheet: I0 = \input 
endmodule
