// Logisim project L11Q2_T-moore.circ as structural Verilog: 1 circuit, main circuit main
module main (
  input  \input ,
  input  Reset,
  output C2,
  output C1,
  output C0,
  output \output 
);

  wire and_1_out, and_2_out, and_3_out, and_4_out, and_5_out, and_6_out, clk_out, not_1_out, not_2_out,
       not_3_out, or_1_out, or_2_out, or_3_out;

  and and_1 (and_1_out, \input , C1, C0);
  and and_2 (and_2_out, C2, \input );
  and and_3 (and_3_out, C1, C0);
  and and_4 (and_4_out, \input , C0);
  not not_1 (not_1_out, \input );
  not not_2 (not_2_out, C1);
  not not_3 (not_3_out, C2);
  or or_1 (or_1_out, and_1_out, C2);
  or or_2 (or_2_out, and_2_out, and_3_out, and_4_out);
  and and_5 (and_5_out, C1, not_1_out);
  or or_3 (or_3_out, and_5_out, and_6_out, C0);
  and and_6 (and_6_out, not_2_out, not_3_out, \input );
  Clock clk (.out(clk_out));
  T_Flip_Flop t_ff_1 (.clk(clk_out), .T(or_1_out), .Q(C2), .reset(Reset));  // open: Qn, preset, en
  T_Flip_Flop t_ff_2 (.clk(clk_out), .T(or_2_out), .Q(C1), .reset(Reset));  // open: Qn, preset, en
  T_Flip_Flop t_ff_3 (.clk(clk_out), .T(or_3_out), .Q(C0), .reset(Reset));  // open: Qn, preset, en

  assign \output  = C2;

  // Other names for the same wires on the sheet: I0 = \input 
endmodule
