// Logisim project L11Q3.circ as structural Verilog: 1 circuit, main circuit main
module main (
  input  [7:0] \input ,
  output [10:0] quotient,
  output [10:0] remainder
);

  wire clock_1_out;
  wire [7:0] register_1_q, register_2_q, register_3_q, register_4_q;
  wire [10:0] adder_1_out, adder_2_out, adder_3_out, bit_extender_1_out, bit_extender_2_out,
       bit_extender_3_out, bit_extender_4_out;

  Clock clock_1 (.out(clock_1_out));
  assign bit_extender_1_out = {{3{1'b0}}, register_1_q};  // Bit_Extender bit_extender_1
  Register register_1 (.D(\input ), .Q(register_1_q), .clk(clock_1_out));  // open: en, clr
  Register register_2 (.D(register_1_q), .Q(register_2_q), .clk(clock_1_out));  // open: en, clr
  Adder #(.width(11)) adder_1 (.a(bit_extender_1_out), .b(bit_extender_2_out), .out(adder_1_out));  // open: cin, cout
  assign bit_extender_2_out = {{3{1'b0}}, register_2_q};  // Bit_Extender bit_extender_2
  Register register_3 (.D(register_2_q), .Q(register_3_q), .clk(clock_1_out));  // open: en, clr
  Adder #(.width(11)) adder_2 (.a(adder_1_out), .b(bit_extender_3_out), .out(adder_2_out));  // open: cin, cout
  assign bit_extender_3_out = {{3{1'b0}}, register_3_q};  // Bit_Extender bit_extender_3
  Register register_4 (.D(register_3_q), .Q(register_4_q), .clk(clock_1_out));  // open: en, clr
  assign bit_extender_4_out = {{3{1'b0}}, register_4_q};  // Bit_Extender bit_extender_4
  Adder #(.width(11)) adder_3 (.a(adder_2_out), .b(bit_extender_4_out), .out(adder_3_out));  // open: cin, cout
  Divider #(.width(11)) divider_1 (.a(adder_3_out), .b(11'h4), .out(quotient), .rem(remainder));  // open: upper
endmodule
