// Logisim project L9Q1_D.circ as structural Verilog: 1 circuit, main circuit main
module main (
);

  wire and_1_out, and_2_out, clock_1_out, d_ff_1_qn, xor_1_out, xor_2_out, xor_3_out;
  wire [3:0] d_ff_1_q;

  Clock clock_1 (.out(clock_1_out));
  D_Flip_Flop d_ff_1 (.clk(clock_1_out), .D(d_ff_1_qn), .Q(d_ff_1_q[0]), .Qn(d_ff_1_qn));  // open: preset, en, reset
  xor xor_1 (xor_1_out, d_ff_1_q[1], d_ff_1_q[0]);
  and and_1 (and_1_out, d_ff_1_q[0], d_ff_1_q[1]);
  D_Flip_Flop d_ff_2 (.clk(clock_1_out), .D(xor_1_out), .Q(d_ff_1_q[1]));  // open: Qn, preset, en, reset
  xor xor_2 (xor_2_out, and_1_out, d_ff_1_q[2]);
  D_Flip_Flop d_ff_3 (.clk(clock_1_out), .D(xor_2_out), .Q(d_ff_1_q[2]));  // open: Qn, preset, en, reset
  and and_2 (and_2_out, and_1_out, d_ff_1_q[2]);
  D_Flip_Flop d_ff_4 (.clk(clock_1_out), .D(xor_3_out), .Q(d_ff_1_q[3]));  // open: Qn, preset, en, reset
  xor xor_3 (xor_3_out, and_2_out, d_ff_1_q[3]);
  Hex_Digit_Display hex_digit_display_1 (.value(d_ff_1_q));  // open: dp
endmodule
