// Logisim project L9Q1_JK.circ as structural Verilog: 1 circuit, main circuit main
module main (
);

  wire and_1_out, and_2_out, clock_1_out;
  wire [3:0] j_k_ff_1_q;

  Clock clock_1 (.out(clock_1_out));
  J_K_Flip_Flop j_k_ff_1 (.J(1'b1), .clk(clock_1_out), .K(1'b1), .Q(j_k_ff_1_q[0]));  // open: Qn, preset, en, reset
  J_K_Flip_Flop j_k_ff_2 (
    .J(j_k_ff_1_q[0]), .clk(clock_1_out), .K(j_k_ff_1_q[0]), .Q(j_k_ff_1_q[1]));  // open: Qn, preset, en, reset
  and and_1 (and_1_out, j_k_ff_1_q[1], j_k_ff_1_q[0]);
  J_K_Flip_Flop j_k_ff_3 (
    .J(and_1_out), .clk(clock_1_out), .K(and_1_out), .Q(j_k_ff_1_q[2]));  // open: Qn, preset, en, reset
  and and_2 (and_2_out, and_1_out, j_k_ff_1_q[2]);
  J_K_Flip_Flop j_k_ff_4 (
    .J(and_2_out), .clk(clock_1_out), .K(and_2_out), .Q(j_k_ff_1_q[3]));  // open: Qn, preset, en, reset
  Hex_Digit_Display hex_digit_display_1 (.value(j_k_ff_1_q));  // open: dp
endmodule
