// Logisim project L9Q1_SR.circ as structural Verilog: 1 circuit, main circuit main
module main (
);

  wire and_1_out, and_2_out, and_3_out, and_4_out, and_5_out, and_6_out, clock_1_out, q1, q2, q3, q4,
       s_r_ff_1_qn, s_r_ff_2_qn, s_r_ff_3_qn, s_r_ff_4_qn;

  Clock clock_1 (.out(clock_1_out));
  S_R_Flip_Flop s_r_ff_1 (
    .S(s_r_ff_1_qn), .clk(clock_1_out), .R(q1), .Q(q1), .Qn(s_r_ff_1_qn));  // open: preset, reset, en
  and and_1 (and_1_out, q1, s_r_ff_2_qn);
  and and_2 (and_2_out, q1, q2);
  S_R_Flip_Flop s_r_ff_2 (
    .S(and_1_out), .clk(clock_1_out), .R(and_2_out), .Q(q2), .Qn(s_r_ff_2_qn));  // open: preset, reset, en
  and and_3 (and_3_out, and_2_out, s_r_ff_3_qn);
  and and_4 (and_4_out, and_2_out, q3);
  S_R_Flip_Flop s_r_ff_3 (
    .S(and_3_out), .clk(clock_1_out), .R(and_4_out), .Q(q3), .Qn(s_r_ff_3_qn));  // open: preset, reset, en
  and and_5 (and_5_out, and_4_out, s_r_ff_4_qn);
  and and_6 (and_6_out, and_4_out, q4);
  S_R_Flip_Flop s_r_ff_4 (
    .S(and_5_out), .clk(clock_1_out), .R(and_6_out), .Q(q4), .Qn(s_r_ff_4_qn));  // open: preset, reset, en
  Hex_Digit_Display hex_digit_display_1 (.value({q4, q3, q2, q1}));  // open: dp
endmodule
