// Logisim project L9Q2.circ as structural Verilog: 1 circuit, main circuit main
module main (
  input  [3:0] read_address_1,
  input  in_2,
  input  [3:0] read_address_2,
  input  [3:0] write_address,
  input  [15:0] value_to_write,
  output [15:0] output1,
  output [15:0] output2
);

  wire clock_1_out, decoder_1_out0, decoder_1_out1, decoder_1_out2, decoder_1_out3, decoder_1_out4,
       decoder_1_out5, decoder_1_out6, decoder_1_out7, decoder_1_out8, decoder_1_out9, decoder_1_out10,
       decoder_1_out11, decoder_1_out12, decoder_1_out13, decoder_1_out14, decoder_1_out15;
  wire [15:0] register_1_q, register_2_q, register_3_q, register_4_q, register_5_q, register_6_q,
       register_7_q, register_8_q, register_9_q, register_10_q, register_11_q, register_12_q, register_13_q,
       register_14_q, register_15_q, register_16_q;

  Clock clock_1 (.out(clock_1_out));
  Decoder #(.select(4)) decoder_1 (
    .out0(decoder_1_out0), .out1(decoder_1_out1), .out2(decoder_1_out2), .out3(decoder_1_out3),
    .out4(decoder_1_out4), .out5(decoder_1_out5), .out6(decoder_1_out6), .out7(decoder_1_out7),
    .out8(decoder_1_out8), .out9(decoder_1_out9), .out10(decoder_1_out10), .out11(decoder_1_out11),
    .out12(decoder_1_out12), .out13(decoder_1_out13), .out14(decoder_1_out14), .out15(decoder_1_out15),
    .sel(write_address), .en(in_2));
  Register #(.width(16)) register_1 (
    .D(value_to_write), .en(decoder_1_out0), .Q(register_1_q), .clk(clock_1_out));  // open: clr
  Register #(.width(16)) register_2 (
    .D(value_to_write), .en(decoder_1_out1), .Q(register_2_q), .clk(clock_1_out));  // open: clr
  Register #(.width(16)) register_3 (
    .D(value_to_write), .en(decoder_1_out2), .Q(register_3_q), .clk(clock_1_out));  // open: clr
  Register #(.width(16)) register_4 (
    .D(value_to_write), .en(decoder_1_out3), .Q(register_4_q), .clk(clock_1_out));  // open: clr
  Register #(.width(16)) register_5 (
    .D(value_to_write), .en(decoder_1_out4), .Q(register_5_q), .clk(clock_1_out));  // open: clr
  Register #(.width(16)) register_6 (
    .D(value_to_write), .en(decoder_1_out5), .Q(register_6_q), .clk(clock_1_out));  // open: clr
  Register #(.width(16)) register_7 (
    .D(value_to_write), .en(decoder_1_out6), .Q(register_7_q), .clk(clock_1_out));  // open: clr
  Register #(.width(16)) register_8 (
    .D(value_to_write), .en(decoder_1_out7), .Q(register_8_q), .clk(clock_1_out));  // open: clr
  Register #(.width(16)) register_9 (
    .D(value_to_write), .en(decoder_1_out8), .Q(register_9_q), .clk(clock_1_out));  // open: clr
  Register #(.width(16)) register_10 (
    .D(value_to_write), .en(decoder_1_out9), .Q(register_10_q), .clk(clock_1_out));  // open: clr
  Register #(.width(16)) register_11 (
    .D(value_to_write), .en(decoder_1_out10), .Q(register_11_q), .clk(clock_1_out));  // open: clr
  Register #(.width(16)) register_12 (
    .D(value_to_write), .en(decoder_1_out11), .Q(register_12_q), .clk(clock_1_out));  // open: clr
  Register #(.width(16)) register_13 (
    .D(value_to_write), .en(decoder_1_out12), .Q(register_13_q), .clk(clock_1_out));  // open: clr
  Register #(.width(16)) register_14 (
    .D(value_to_write), .en(decoder_1_out13), .Q(register_14_q), .clk(clock_1_out));  // open: clr
  Register #(.width(16)) register_15 (
    .D(value_to_write), .en(decoder_1_out14), .Q(register_15_q), .clk(clock_1_out));  // open: clr
  Register #(.width(16)) register_16 (
    .D(value_to_write), .en(decoder_1_out15), .Q(register_16_q), .clk(clock_1_out));  // open: clr
  Multiplexer #(.select(4), .width(16)) multiplexer_1 (
    .in0(register_1_q), .in1(register_2_q), .in2(register_3_q), .in3(register_4_q), .in4(register_5_q),
    .in5(register_6_q), .in6(register_7_q), .in7(register_8_q), .in8(register_9_q), .in9(register_10_q),
    .in10(register_11_q), .in11(register_12_q), .in12(register_13_q), .in13(register_14_q),
    .in14(register_15_q), .in15(register_16_q), .out(output1), .sel(read_address_1));  // open: en
  Multiplexer #(.select(4), .width(16)) multiplexer_2 (
    .in0(register_1_q), .in1(register_2_q), .in2(register_3_q), .in3(register_4_q), .in4(register_5_q),
    .in5(register_6_q), .in6(register_7_q), .in7(register_8_q), .in8(register_9_q), .in9(register_10_q),
    .in10(register_11_q), .in11(register_12_q), .in12(register_13_q), .in13(register_14_q),
    .in14(register_15_q), .in15(register_16_q), .out(output2), .sel(read_address_2));  // open: en
endmodule
