// Logisim project L9Q3.circ as structural Verilog: 3 circuits, main circuit main
module main (
  input  [15:0] in_1,
  input  in_2,
  input  [3:0] write_address,
  input  [1:0] operation,
  input  [3:0] read_1,
  input  [3:0] read_2,
  input  clear,
  output [15:0] out_8
);

  wire clock_1_out;
  wire [15:0] multiplexer_1_out, n16reg_1_output1, n16reg_1_output2;

  Multiplexer #(.width(16)) multiplexer_1 (.in0(in_1), .in1(out_8), .out(multiplexer_1_out), .sel(in_2));  // open: en
  Clock clock_1 (.out(clock_1_out));
  _16reg u_16reg_1 (
    .read_address_1(read_1), .read_address_2(read_2), .clk(clock_1_out), .clear(clear),
    .value_to_write(multiplexer_1_out), .write_address(write_address), .output1(n16reg_1_output1),
    .output2(n16reg_1_output2));
  ALU alu_1 (.i1(n16reg_1_output1), .i2(n16reg_1_output2), .sel(operation), .\output (out_8));
endmodule

// 16 * 16 REG
module _16reg (
  input  [3:0] read_address_1,
  input  [3:0] read_address_2,
  input  [3:0] write_address,
  input  [15:0] value_to_write,
  input  clk,
  input  clear,
  output [15:0] output1,
  output [15:0] output2
);

  wire decoder_1_out0, decoder_1_out1, decoder_1_out2, decoder_1_out3, decoder_1_out4, decoder_1_out5,
       decoder_1_out6, decoder_1_out7, decoder_1_out8, decoder_1_out9, decoder_1_out10, decoder_1_out11,
       decoder_1_out12, decoder_1_out13, decoder_1_out14, decoder_1_out15;
  wire [15:0] register_1_q, register_2_q, register_3_q, register_4_q, register_5_q, register_6_q,
       register_7_q, register_8_q, register_9_q, register_10_q, register_11_q, register_12_q, register_13_q,
       register_14_q, register_15_q, register_16_q;

  Decoder #(.select(4)) decoder_1 (
    .out0(decoder_1_out0), .out1(decoder_1_out1), .out2(decoder_1_out2), .out3(decoder_1_out3),
    .out4(decoder_1_out4), .out5(decoder_1_out5), .out6(decoder_1_out6), .out7(decoder_1_out7),
    .out8(decoder_1_out8), .out9(decoder_1_out9), .out10(decoder_1_out10), .out11(decoder_1_out11),
    .out12(decoder_1_out12), .out13(decoder_1_out13), .out14(decoder_1_out14), .out15(decoder_1_out15),
    .sel(write_address));  // open: en
  Register #(.width(16)) register_1 (.D(value_to_write), .en(decoder_1_out0), .Q(register_1_q), .clk(clk), .clr(clear));
  Register #(.width(16)) register_2 (.D(value_to_write), .en(decoder_1_out1), .Q(register_2_q), .clk(clk), .clr(clear));
  Register #(.width(16)) register_3 (.D(value_to_write), .en(decoder_1_out2), .Q(register_3_q), .clk(clk), .clr(clear));
  Register #(.width(16)) register_4 (.D(value_to_write), .en(decoder_1_out3), .Q(register_4_q), .clk(clk), .clr(clear));
  Register #(.width(16)) register_5 (.D(value_to_write), .en(decoder_1_out4), .Q(register_5_q), .clk(clk), .clr(clear));
  Register #(.width(16)) register_6 (.D(value_to_write), .en(decoder_1_out5), .Q(register_6_q), .clk(clk), .clr(clear));
  Register #(.width(16)) register_7 (.D(value_to_write), .en(decoder_1_out6), .Q(register_7_q), .clk(clk), .clr(clear));
  Register #(.width(16)) register_8 (.D(value_to_write), .en(decoder_1_out7), .Q(register_8_q), .clk(clk), .clr(clear));
  Register #(.width(16)) register_9 (.D(value_to_write), .en(decoder_1_out8), .Q(register_9_q), .clk(clk), .clr(clear));
  Register #(.width(16)) register_10 (
    .D(value_to_write), .en(decoder_1_out9), .Q(register_10_q), .clk(clk), .clr(clear));
  Register #(.width(16)) register_11 (
    .D(value_to_write), .en(decoder_1_out10), .Q(register_11_q), .clk(clk), .clr(clear));
  Register #(.width(16)) register_12 (
    .D(value_to_write), .en(decoder_1_out11), .Q(register_12_q), .clk(clk), .clr(clear));
  Register #(.width(16)) register_13 (
    .D(value_to_write), .en(decoder_1_out12), .Q(register_13_q), .clk(clk), .clr(clear));
  Register #(.width(16)) register_14 (
    .D(value_to_write), .en(decoder_1_out13), .Q(register_14_q), .clk(clk), .clr(clear));
  Register #(.width(16)) register_15 (
    .D(value_to_write), .en(decoder_1_out14), .Q(register_15_q), .clk(clk), .clr(clear));
  Register #(.width(16)) register_16 (
    .D(value_to_write), .en(decoder_1_out15), .Q(register_16_q), .clk(clk), .clr(clear));
  Multiplexer #(.select(4), .width(16)) multiplexer_1 (
    .in0(register_1_q), .in1(register_2_q), .in2(register_3_q), .in3(register_4_q), .in4(register_5_q),
    .in5(register_6_q), .in6(register_7_q), .in7(register_8_q), .in8(register_9_q), .in9(register_10_q),
    .in10(register_11_q), .in11(register_12_q), .in12(register_13_q), .in13(register_14_q),
    .in14(register_15_q), .in15(register_16_q), .out(output1), .sel(read_address_1));  // open: en
  Multiplexer #(.select(4), .width(16)) multiplexer_2 (
    .in0(register_1_q), .in1(register_2_q), .in2(register_3_q), .in3(register_4_q), .in4(register_5_q),
    .in5(register_6_q), .in6(register_7_q), .in7(register_8_q), .in8(register_9_q), .in9(register_10_q),
    .in10(register_11_q), .in11(register_12_q), .in12(register_13_q), .in13(register_14_q),
    .in14(register_15_q), .in15(register_16_q), .out(output2), .sel(read_address_2));  // open: en
endmodule

module ALU (
  input  [15:0] i1,
  input  [15:0] i2,
  input  [1:0] sel,
  output [15:0] \output 
);

  wire [15:0] adder_1_out, and_1_out, or_1_out, subtractor_1_out;

  Adder #(.width(16)) adder_1 (.a(i1), .b(i2), .out(adder_1_out));  // open: cin, cout
  Subtractor #(.width(16)) subtractor_1 (.a(i1), .b(i2), .out(subtractor_1_out));  // open: bin, bout
  assign and_1_out = i1 & i2;  // AND_Gate and_1, 16 bits wide
  assign or_1_out = i1 | i2;  // OR_Gate or_1, 16 bits wide
  Multiplexer #(.select(2), .width(16)) multiplexer_1 (
    .in0(adder_1_out), .in1(subtractor_1_out), .in2(and_1_out), .in3(or_1_out), .out(\output ), .sel(sel));  // open: en
endmodule
