// Logisim project p5.circ as structural Verilog: 1 circuit, main circuit main
module main (
  input  in_1,
  input  in_2,
  input  in_3,
  input  in_4,
  output out_5
);

  wire transistor_5_out, transistor_6_out, transistor_7_out;

  Transistor #(.\type ("n")) transistor_1 (.in(1'b1), .out(out_5), .gate(in_1));
  Transistor #(.\type ("n")) transistor_2 (.in(1'b1), .out(out_5), .gate(in_2));
  Transistor #(.\type ("n")) transistor_3 (.in(1'b1), .out(out_5), .gate(in_3));
  Transistor transistor_4 (.in(transistor_5_out), .out(out_5), .gate(in_1));
  Transistor transistor_5 (.in(transistor_6_out), .out(transistor_5_out), .gate(in_2));
  Transistor transistor_6 (.in(transistor_7_out), .out(transistor_6_out), .gate(in_3));
  Transistor transistor_7 (.in(1'b0), .out(transistor_7_out), .gate(in_4));
  Transistor #(.\type ("n")) transistor_8 (.in(1'b1), .out(out_5), .gate(in_4));
endmodule
