// Logisim project p1.circ as structural Verilog: 1 circuit, main circuit main
module main (
  input  in_1,
  input  in_2,
  input  in_3,
  input  in_4,
  input  in_5,
  input  in_6,
  input  in_7,
  input  in_8,
  output OR,
  output NAND
);

  wire transistor_2_out, transistor_3_out, transistor_4_out, transistor_6_out, transistor_7_out,
       transistor_8_out;

  Pull_Resistor #(.pull(1)) pull_resistor_1 (.node(OR));
  Transistor transistor_1 (.in(transistor_2_out), .out(OR), .gate(in_1));
  Transistor transistor_2 (.in(transistor_3_out), .out(transistor_2_out), .gate(in_3));
  Transistor transistor_3 (.in(transistor_4_out), .out(transistor_3_out), .gate(in_5));
  Transistor transistor_4 (.in(1'b0), .out(transistor_4_out), .gate(in_7));
  Pull_Resistor #(.pull(1)) pull_resistor_2 (.node(NAND));
  Transistor #(.\type ("n")) transistor_5 (.in(transistor_6_out), .out(NAND), .gate(in_2));
  Transistor #(.\type ("n")) transistor_6 (.in(transistor_7_out), .out(transistor_6_out), .gate(in_4));
  Transistor #(.\type ("n")) transistor_7 (.in(transistor_8_out), .out(transistor_7_out), .gate(in_6));
  Transistor #(.\type ("n")) transistor_8 (.in(1'b0), .out(transistor_8_out), .gate(in_8));
endmodule
