// Logisim project p2.circ as structural Verilog: 5 circuits, main circuit main
module main (
  input  in_1,
  input  in_2,
  input  in_3,
  input  in_4,
  input  in_5,
  output AND,
  output NAND,
  output NOR,
  output OR
);

  wire transistor_2_out, transistor_3_out, transistor_4_out, transistor_5_out, transistor_6_out,
       transistor_17_out, transistor_18_out, transistor_19_out, transistor_20_out, transistor_21_out;

  Transistor #(.\type ("n")) transistor_1 (.in(transistor_2_out), .out(NAND), .gate(in_1));
  Pull_Resistor #(.pull(1)) pull_resistor_1 (.node(NAND));
  Transistor #(.\type ("n")) transistor_2 (.in(transistor_3_out), .out(transistor_2_out), .gate(in_2));
  Transistor #(.\type ("n")) transistor_3 (.in(transistor_4_out), .out(transistor_3_out), .gate(in_3));
  Transistor #(.\type ("n")) transistor_4 (.in(transistor_5_out), .out(transistor_4_out), .gate(in_4));
  Transistor #(.\type ("n")) transistor_5 (.in(1'b0), .out(transistor_5_out), .gate(in_5));
  Transistor #(.\type ("n")) transistor_6 (.in(1'b0), .out(transistor_6_out), .gate(in_1));
  Transistor #(.\type ("n")) transistor_7 (.in(1'b0), .out(NOR), .gate(in_1));
  Transistor #(.\type ("n")) transistor_8 (.in(1'b0), .out(NOR), .gate(in_2));
  Pull_Resistor #(.pull(1)) pull_resistor_2 (.node(transistor_6_out));
  Transistor #(.\type ("n")) transistor_9 (.in(1'b0), .out(transistor_6_out), .gate(in_3));
  Transistor #(.\type ("n")) transistor_10 (.in(1'b0), .out(transistor_6_out), .gate(in_2));
  Pull_Resistor #(.pull(1)) pull_resistor_3 (.node(NOR));
  Transistor #(.\type ("n")) transistor_11 (.in(1'b0), .out(NOR), .gate(in_3));
  Transistor #(.\type ("n")) transistor_12 (.in(1'b0), .out(transistor_6_out), .gate(in_4));
  Transistor #(.\type ("n")) transistor_13 (.in(1'b0), .out(NOR), .gate(in_4));
  Transistor #(.\type ("n")) transistor_14 (.in(1'b0), .out(transistor_6_out), .gate(in_5));
  Transistor #(.\type ("n")) transistor_15 (.in(1'b0), .out(NOR), .gate(in_5));
  Pull_Resistor #(.pull(1)) pull_resistor_4 (.node(OR));
  Transistor #(.\type ("n")) transistor_16 (.in(1'b0), .out(OR), .gate(transistor_6_out));
  Transistor #(.\type ("n")) transistor_17 (.in(transistor_18_out), .out(transistor_17_out), .gate(in_1));
  Pull_Resistor #(.pull(1)) pull_resistor_5 (.node(transistor_17_out));
  Transistor #(.\type ("n")) transistor_18 (.in(transistor_19_out), .out(transistor_18_out), .gate(in_2));
  Transistor #(.\type ("n")) transistor_19 (.in(transistor_20_out), .out(transistor_19_out), .gate(in_3));
  Transistor #(.\type ("n")) transistor_20 (.in(transistor_21_out), .out(transistor_20_out), .gate(in_4));
  Transistor #(.\type ("n")) transistor_21 (.in(1'b0), .out(transistor_21_out), .gate(in_5));
  Pull_Resistor #(.pull(1)) pull_resistor_6 (.node(AND));
  Transistor #(.\type ("n")) transistor_22 (.in(1'b0), .out(AND), .gate(transistor_17_out));

  // Other names for the same wires on the sheet: A = in_1; B = in_2; C = in_3; D = in_4; E = in_5
endmodule

module _5NAND (
  input  in_1,
  input  in_2,
  input  in_3,
  input  in_4,
  input  in_5,
  output out_6
);

  wire transistor_2_out, transistor_3_out, transistor_4_out, transistor_5_out;

  Pull_Resistor #(.pull(1)) pull_resistor_1 (.node(out_6));
  Transistor #(.\type ("n")) transistor_1 (.in(transistor_2_out), .out(out_6), .gate(in_1));
  Transistor #(.\type ("n")) transistor_2 (.in(transistor_3_out), .out(transistor_2_out), .gate(in_2));
  Transistor #(.\type ("n")) transistor_3 (.in(transistor_4_out), .out(transistor_3_out), .gate(in_3));
  Transistor #(.\type ("n")) transistor_4 (.in(transistor_5_out), .out(transistor_4_out), .gate(in_4));
  Transistor #(.\type ("n")) transistor_5 (.in(1'b0), .out(transistor_5_out), .gate(in_5));
endmodule

module _5NOR (
  input  in_1,
  input  in_2,
  input  in_3,
  input  in_4,
  input  in_5,
  output out_6
);

  Transistor #(.\type ("n")) transistor_1 (.in(1'b0), .out(out_6), .gate(in_1));
  Pull_Resistor #(.pull(1)) pull_resistor_1 (.node(out_6));
  Transistor #(.\type ("n")) transistor_2 (.in(1'b0), .out(out_6), .gate(in_2));
  Transistor #(.\type ("n")) transistor_3 (.in(1'b0), .out(out_6), .gate(in_3));
  Transistor #(.\type ("n")) transistor_4 (.in(1'b0), .out(out_6), .gate(in_4));
  Transistor #(.\type ("n")) transistor_5 (.in(1'b0), .out(out_6), .gate(in_5));
endmodule

module _5AND (
  input  in_1,
  input  in_2,
  input  in_3,
  input  in_4,
  input  in_5,
  output out_6
);

  wire transistor_2_out, transistor_3_out, transistor_4_out, transistor_5_out;

  Transistor #(.\type ("n")) transistor_1 (.in(transistor_2_out), .out(out_6), .gate(in_1));
  Pull_Resistor pull_resistor_1 (.node(out_6));
  Transistor #(.\type ("n")) transistor_2 (.in(transistor_3_out), .out(transistor_2_out), .gate(in_2));
  Transistor #(.\type ("n")) transistor_3 (.in(transistor_4_out), .out(transistor_3_out), .gate(in_3));
  Transistor #(.\type ("n")) transistor_4 (.in(transistor_5_out), .out(transistor_4_out), .gate(in_4));
  Transistor #(.\type ("n")) transistor_5 (.in(1'b1), .out(transistor_5_out), .gate(in_5));
endmodule

module _5OR (
  input  in_1,
  input  in_2,
  input  in_3,
  input  in_4,
  input  in_5,
  output out_6
);

  Transistor #(.\type ("n")) transistor_1 (.in(1'b1), .out(out_6), .gate(in_1));
  Pull_Resistor pull_resistor_1 (.node(out_6));
  Transistor #(.\type ("n")) transistor_2 (.in(1'b1), .out(out_6), .gate(in_3));
  Transistor #(.\type ("n")) transistor_3 (.in(1'b1), .out(out_6), .gate(in_2));
  Transistor #(.\type ("n")) transistor_4 (.in(1'b1), .out(out_6), .gate(in_4));
  Transistor #(.\type ("n")) transistor_5 (.in(1'b1), .out(out_6), .gate(in_5));
endmodule
