// Logisim project p6.circ as structural Verilog: 1 circuit, main circuit main
module main (
  input  A,
  input  B,
  input  C,
  input  D,
  output out_5
);

  wire and_1_out;

  and and_1 (and_1_out, B, C);
  or or_1 (out_5, A, and_1_out, D);
endmodule
