// Logisim project p1.circ as structural Verilog: 1 circuit, main circuit main
module main (
  input  w,
  input  x,
  input  y,
  input  z,
  output out_5
);

  wire and_1_out, and_2_out, and_3_out, and_4_out, minus_w, minus_x, minus_y, minus_z;

  not not_1 (minus_w, w);
  and and_1 (and_1_out, w, minus_x, minus_y);
  and and_2 (and_2_out, y, minus_w, minus_z);
  and and_3 (and_3_out, y, x, z);
  and and_4 (and_4_out, y, x, w);
  not not_2 (minus_x, x);
  not not_3 (minus_y, y);
  or or_1 (out_5, and_1_out, and_2_out, and_3_out, and_4_out);
  not not_4 (minus_z, z);
endmodule
