// Logisim project p10.circ as structural Verilog: 1 circuit, main circuit main
module main (
  input  a0,
  input  b0,
  input  a1,
  input  b1,
  output s0,
  output s1
);

  wire and_1_out;

  xor xor_1 (s0, a0, b0);
  and and_1 (and_1_out, b0, a0);
  ExactlyOne xor_2 (.out(s1), .in0(and_1_out), .in1(a1), .in2(b1));
endmodule
