// Logisim project p2.circ as structural Verilog: 1 circuit, main circuit main
module main (
  input  i1,
  input  i0,
  output d0,
  output d1,
  output d2,
  output d3
);

  wire not_1_out, not_2_out;

  not not_1 (not_1_out, i0);
  not not_2 (not_2_out, i1);
  and and_1 (d0, not_2_out, not_1_out);
  and and_2 (d1, i1, not_1_out);
  and and_3 (d2, not_2_out, i0);
  and and_4 (d3, i1, i0);
endmodule
