// Logisim project p4.circ as structural Verilog: 1 circuit, main circuit main
module main (
  input  s0,
  input  s1,
  input  s2,
  input  s3,
  input  D,
  input  C,
  input  B,
  input  A,
  output out_9
);

  wire and_1_out, and_2_out, and_3_out, and_4_out, and_5_out, and_6_out, minus_s0, minus_s1, minus_s2,
       minus_s3, not_5_out, not_6_out;

  not not_1 (minus_s0, s0);
  not not_2 (minus_s1, s1);
  not not_3 (minus_s2, s2);
  not not_4 (minus_s3, s3);
  and and_1 (and_1_out, minus_s0, minus_s1);
  and and_2 (and_2_out, minus_s0, minus_s2);
  and and_3 (and_3_out, and_2_out, and_1_out, D);
  not not_5 (not_5_out, and_1_out);
  not not_6 (not_6_out, and_2_out);
  and and_4 (and_4_out, not_6_out, and_1_out, C);
  or or_1 (out_9, and_3_out, and_4_out, and_5_out, and_6_out);
  and and_5 (and_5_out, and_2_out, not_5_out, B);
  and and_6 (and_6_out, not_6_out, not_5_out, A);
endmodule
