// Logisim project p5.circ as structural Verilog: 2 circuits, main circuit main
module main (
  input  a0,
  input  b0,
  input  a1,
  input  b1,
  input  a2,
  input  b2,
  input  a3,
  input  b3,
  input  in_9,
  output d3,
  output d2,
  output d1,
  output d0
);

  BLOCKA blocka_1 (.A(a3), .B(b3), .s0(in_9), .o0(d3));
  BLOCKA blocka_2 (.A(a2), .B(b2), .s0(in_9), .o0(d2));
  BLOCKA blocka_3 (.A(a1), .B(b1), .s0(in_9), .o0(d1));
  BLOCKA blocka_4 (.A(a0), .B(b0), .s0(in_9), .o0(d0));
endmodule

module BLOCKA (
  input  A,
  input  B,
  input  s0,
  output o0
);

  wire and_1_out, and_2_out, not_1_out;

  not not_1 (not_1_out, s0);
  and and_1 (and_1_out, A, not_1_out);
  and and_2 (and_2_out, B, s0);
  or or_1 (o0, and_1_out, and_2_out);
endmodule
