// Logisim project p6.circ as structural Verilog: 2 circuits, main circuit main
module main (
  input  a3,
  input  b3,
  input  c3,
  input  d3,
  input  a2,
  input  b2,
  input  c2,
  input  d2,
  input  a1,
  input  b1,
  input  c1,
  input  d1,
  input  a0,
  input  b0,
  input  c0,
  input  d0,
  input  s1,
  input  s0,
  output out_19,
  output out_20,
  output out_21,
  output out_22
);

  BLOCKA blocka_1 (.in_1(a3), .in_2(b3), .in_3(c3), .in_4(d3), .in_5(s1), .in_6(s0), .out_7(out_19));
  BLOCKA blocka_2 (.in_1(a2), .in_2(b2), .in_3(c2), .in_4(d2), .in_5(s1), .in_6(s0), .out_7(out_20));
  BLOCKA blocka_3 (.in_1(a1), .in_2(b1), .in_3(c1), .in_4(d1), .in_5(s1), .in_6(s0), .out_7(out_21));
  BLOCKA blocka_4 (.in_1(a0), .in_2(b0), .in_3(c0), .in_4(d0), .in_5(s1), .in_6(s0), .out_7(out_22));
endmodule

module BLOCKA (
  input  in_1,
  input  in_2,
  input  in_3,
  input  in_4,
  input  in_5,
  input  in_6,
  output out_7
);

  wire and_1_out, and_2_out, and_3_out, and_4_out, not_1_out, not_2_out;

  not not_1 (not_1_out, in_5);
  not not_2 (not_2_out, in_6);
  and and_1 (and_1_out, in_1, not_1_out, not_2_out);
  and and_2 (and_2_out, in_2, not_1_out, in_6);
  and and_3 (and_3_out, in_3, in_5, not_2_out);
  and and_4 (and_4_out, in_4, in_5, in_6);
  or or_1 (out_7, and_1_out, and_2_out, and_3_out, and_4_out);
endmodule
