// Logisim project p7.circ as structural Verilog: 1 circuit, main circuit main
module main (
  input  a0,
  input  s0,
  input  s1,
  input  s2,
  input  a1,
  input  a2,
  input  a3,
  input  a4,
  input  a5,
  input  a6,
  input  a7,
  output out_12
);

  wire and_1_out, and_2_out, and_3_out, and_4_out, and_5_out, and_6_out, and_7_out, and_8_out, minus_s0,
       minus_s1, minus_s2;

  and and_1 (and_1_out, a0, minus_s2, minus_s1, minus_s0);
  and and_2 (and_2_out, a2, minus_s2, s1, minus_s0);
  and and_3 (and_3_out, a4, s2, minus_s1, minus_s0);
  and and_4 (and_4_out, a6, s2, s1, minus_s0);
  and and_5 (and_5_out, a1, minus_s2, minus_s1, s0);
  and and_6 (and_6_out, a3, minus_s2, s1, s0);
  and and_7 (and_7_out, a5, s2, minus_s1, s0);
  and and_8 (and_8_out, a7, s2, s1, s0);
  not not_1 (minus_s0, s0);
  or or_1 (out_12, and_1_out, and_5_out, and_2_out, and_6_out, and_3_out, and_7_out, and_4_out, and_8_out);
  not not_2 (minus_s1, s1);
  not not_3 (minus_s2, s2);
endmodule
