// Logisim project p8.circ as structural Verilog: 2 circuits, main circuit main
module main (
  input  s0,
  input  s1,
  input  s2,
  input  s3,
  input  in_5,
  input  in_6,
  input  in_7,
  input  in_8,
  input  in_9,
  input  in_10,
  input  in_11,
  input  in_12,
  input  in_13,
  input  in_14,
  input  in_15,
  input  in_16,
  input  in_17,
  input  in_18,
  input  in_19,
  input  in_20,
  output out_21
);

  wire and_1_out, and_2_out, n8x1_1_out_12, n8x1_2_out_12, not_1_out;

  _8x1 u_8x1_1 (
    .a0(in_5), .a1(in_6), .a2(in_7), .a3(in_8), .a4(in_9), .a5(in_10), .a6(in_11), .a7(in_12), .s0(s0),
    .s1(s1), .s2(s2), .out_12(n8x1_1_out_12));
  _8x1 u_8x1_2 (
    .a0(in_13), .a1(in_14), .a2(in_15), .a3(in_16), .a4(in_17), .a5(in_18), .a6(in_19), .a7(in_20), .s0(s0),
    .s1(s1), .s2(s2), .out_12(n8x1_2_out_12));
  not not_1 (not_1_out, s3);
  and and_1 (and_1_out, n8x1_1_out_12, not_1_out);
  and and_2 (and_2_out, n8x1_2_out_12, s3);
  or or_1 (out_21, and_1_out, and_2_out);
endmodule

module _8x1 (
  input  a0,
  input  s0,
  input  s1,
  input  s2,
  input  a1,
  input  a2,
  input  a3,
  input  a4,
  input  a5,
  input  a6,
  input  a7,
  output out_12
);

  wire and_1_out, and_2_out, and_3_out, and_4_out, and_5_out, and_6_out, and_7_out, and_8_out, minus_s0,
       minus_s1, minus_s2;

  and and_1 (and_1_out, a0, minus_s2, minus_s1, minus_s0);
  and and_2 (and_2_out, a2, minus_s2, s1, minus_s0);
  and and_3 (and_3_out, a4, s2, minus_s1, minus_s0);
  and and_4 (and_4_out, a6, s2, s1, minus_s0);
  and and_5 (and_5_out, a1, minus_s2, minus_s1, s0);
  and and_6 (and_6_out, a3, minus_s2, s1, s0);
  and and_7 (and_7_out, a5, s2, minus_s1, s0);
  and and_8 (and_8_out, a7, s2, s1, s0);
  not not_1 (minus_s0, s0);
  or or_1 (out_12, and_1_out, and_5_out, and_2_out, and_6_out, and_3_out, and_7_out, and_4_out, and_8_out);
  not not_2 (minus_s1, s1);
  not not_3 (minus_s2, s2);
endmodule
