// Logisim project p9.circ as structural Verilog: 3 circuits, main circuit main
module main (
  input  a0,
  input  a1,
  input  b0,
  input  b1,
  output s0,
  output s1,
  output carry
);

  wire half_adder_1_c0;

  half_adder half_adder_1 (.in_1(a0), .in_2(b0), .s0(s0), .c0(half_adder_1_c0));
  full_adder full_adder_1 (.in_1(a1), .in_2(half_adder_1_c0), .in_3(b1), .s0(s1), .c0(carry));
endmodule

module half_adder (
  input  in_1,
  input  in_2,
  output s0,
  output c0
);

  xor xor_1 (s0, in_1, in_2);
  and and_1 (c0, in_1, in_2);
endmodule

module full_adder (
  input  in_1,
  input  in_2,
  input  in_3,
  output s0,
  output c0
);

  wire and_1_out, and_2_out, xor_1_out;

  and and_1 (and_1_out, in_1, in_2);
  xor xor_1 (xor_1_out, in_1, in_2);
  xor xor_2 (s0, xor_1_out, in_3);
  and and_2 (and_2_out, xor_1_out, in_3);
  or or_1 (c0, and_2_out, and_1_out);
endmodule
