// Logisim project p1.circ as structural Verilog: 5 circuits, main circuit main
module main (
  input  [3:0] A,
  input  [3:0] B,
  input  [1:0] S,
  output [3:0] out_4
);

  wire [3:0] and_1_d0, n4bitadder_sub_1_d0, or_1_d0;

  _4bitadder_sub u_4bitadder_sub_1 (
    .a3(A[3]), .b3(B[3]), .a2(A[2]), .b2(B[2]), .a1(A[1]), .b1(B[1]), .a0(A[0]), .b0(B[0]),
    .d3(n4bitadder_sub_1_d0[3]), .d2(n4bitadder_sub_1_d0[2]), .d1(n4bitadder_sub_1_d0[1]),
    .d0(n4bitadder_sub_1_d0[0]), .k(S[0]));  // open: out_10
  AND and_1 (
    .a0(A[0]), .b0(B[0]), .a1(A[1]), .b1(B[1]), .a2(B[2]), .b2(A[2]), .a3(B[3]), .b3(A[3]), .d0(and_1_d0[0]),
    .d1(and_1_d0[1]), .d2(and_1_d0[2]), .d3(and_1_d0[3]));
  OR or_1 (
    .a0(A[0]), .b0(B[0]), .a1(A[1]), .b1(B[1]), .a2(B[2]), .b2(A[2]), .a3(B[3]), .b3(A[3]), .d0(or_1_d0[0]),
    .d1(or_1_d0[1]), .d2(or_1_d0[2]), .d3(or_1_d0[3]));
  Multiplexer #(.select(2), .width(4), .enable("false")) multiplexer_1 (
    .in0(n4bitadder_sub_1_d0), .in1(n4bitadder_sub_1_d0), .in2(and_1_d0), .in3(or_1_d0), .out(out_4), .sel(S));
endmodule

module AND (
  input  a0,
  input  b0,
  input  a1,
  input  b1,
  input  a2,
  input  b2,
  input  a3,
  input  b3,
  output d0,
  output d1,
  output d2,
  output d3
);

  and and_1 (d0, a0, b0);
  and and_2 (d1, a1, b1);
  and and_3 (d2, a2, b2);
  and and_4 (d3, a3, b3);
endmodule

module OR (
  input  a0,
  input  b0,
  input  a1,
  input  b1,
  input  a2,
  input  b2,
  input  a3,
  input  b3,
  output d0,
  output d1,
  output d2,
  output d3
);

  or or_1 (d0, a0, b0);
  or or_2 (d1, a1, b1);
  or or_3 (d2, a2, b2);
  or or_4 (d3, a3, b3);
endmodule

module FullAdder (
  input  a0,
  input  b0,
  input  cin,
  output s,
  output cout
);

  wire and_1_out, and_2_out, xor_1_out;

  xor xor_1 (xor_1_out, a0, b0);
  and and_1 (and_1_out, cin, xor_1_out);
  xor xor_2 (s, xor_1_out, cin);
  and and_2 (and_2_out, a0, b0);
  or or_1 (cout, and_1_out, and_2_out);
endmodule

module _4bitadder_sub (
  input  b3,
  input  b2,
  input  b1,
  input  b0,
  input  k,
  input  a3,
  input  a2,
  input  a1,
  input  a0,
  output out_10,
  output d3,
  output d2,
  output d1,
  output d0
);

  wire fulladder_2_cout, fulladder_3_cout, fulladder_4_cout, xor_1_out, xor_2_out, xor_3_out, xor_4_out;

  FullAdder fulladder_1 (.a0(fulladder_2_cout), .b0(xor_1_out), .cin(a3), .s(d3), .cout(out_10));
  xor xor_1 (xor_1_out, b3, k);
  xor xor_2 (xor_2_out, b2, k);
  FullAdder fulladder_2 (.a0(fulladder_3_cout), .b0(xor_2_out), .cin(a2), .s(d2), .cout(fulladder_2_cout));
  xor xor_3 (xor_3_out, b1, k);
  FullAdder fulladder_3 (.a0(fulladder_4_cout), .b0(xor_3_out), .cin(a1), .s(d1), .cout(fulladder_3_cout));
  xor xor_4 (xor_4_out, b0, k);
  FullAdder fulladder_4 (.a0(k), .b0(xor_4_out), .cin(a0), .s(d0), .cout(fulladder_4_cout));
endmodule
