// Logisim project p2.circ as structural Verilog: 3 circuits, main circuit main
module main (
  input  [9:0] in_1,
  input  [9:0] in_2,
  input  in_3,
  input  in_4,
  output [9:0] out_5,
  output out_6
);

  wire n4bitadeer_sub_2_out_10, n4bitadeer_sub_3_out_10;

  _4bitadeer_sub u_4bitadeer_sub_1 (
    .a2(in_3), .b2(in_3), .a1(in_1[9]), .b1(in_2[9]), .a0(in_1[8]), .b0(in_2[8]), .d2(out_6), .d1(out_5[9]),
    .d0(out_5[8]), .k(n4bitadeer_sub_2_out_10));  // open: out_10, a3, b3, d3
  _4bitadeer_sub u_4bitadeer_sub_2 (
    .out_10(n4bitadeer_sub_2_out_10), .a3(in_1[7]), .b3(in_2[7]), .a2(in_1[6]), .b2(in_2[6]), .a1(in_1[5]),
    .b1(in_2[5]), .a0(in_1[4]), .b0(in_2[4]), .d3(out_5[7]), .d2(out_5[6]), .d1(out_5[5]), .d0(out_5[4]),
    .k(n4bitadeer_sub_3_out_10));
  _4bitadeer_sub u_4bitadeer_sub_3 (
    .out_10(n4bitadeer_sub_3_out_10), .a3(in_1[3]), .b3(in_2[3]), .a2(in_1[2]), .b2(in_2[2]), .a1(in_1[1]),
    .b1(in_2[1]), .a0(in_1[0]), .b0(in_2[0]), .d3(out_5[3]), .d2(out_5[2]), .d1(out_5[1]), .d0(out_5[0]),
    .k(in_4));
endmodule

module FullAdder (
  input  a0,
  input  b0,
  input  cin,
  output s,
  output cout
);

  wire and_1_out, and_2_out, xor_1_out;

  xor xor_1 (xor_1_out, a0, b0);
  and and_1 (and_1_out, cin, xor_1_out);
  xor xor_2 (s, xor_1_out, cin);
  and and_2 (and_2_out, a0, b0);
  or or_1 (cout, and_1_out, and_2_out);
endmodule

module _4bitadeer_sub (
  input  b3,
  input  b2,
  input  b1,
  input  b0,
  input  k,
  input  a3,
  input  a2,
  input  a1,
  input  a0,
  output out_10,
  output d3,
  output d2,
  output d1,
  output d0
);

  wire fulladder_2_cout, fulladder_3_cout, fulladder_4_cout;

  FullAdder fulladder_1 (.a0(fulladder_2_cout), .b0(b3), .cin(a3), .s(d3), .cout(out_10));
  FullAdder fulladder_2 (.a0(fulladder_3_cout), .b0(b2), .cin(a2), .s(d2), .cout(fulladder_2_cout));
  FullAdder fulladder_3 (.a0(fulladder_4_cout), .b0(b1), .cin(a1), .s(d1), .cout(fulladder_3_cout));
  FullAdder fulladder_4 (.a0(k), .b0(b0), .cin(a0), .s(d0), .cout(fulladder_4_cout));
endmodule
