// Logisim project p3.circ as structural Verilog: 1 circuit, main circuit main
module main (
  input  [15:0] in_1,
  input  [15:0] in_2,
  input  [3:0] in_3,
  output out_4,
  output [15:0] out_5,
  output [15:0] _16_31multiplier_remainder_overflow_in_adder_negative_in_subtractor
);

  wire adder_1_cout, comparator_1_lt, subtractor_1_bout;
  wire [15:0] adder_1_out, and_1_out, bit_extender_3_out, divider_1_out, i0, i1, i2, i3, multiplier_1_out,
       nand_1_out, nor_1_out, or_1_out, subtractor_1_out, xnor_1_out, xor_1_out;

  Adder #(.width(16)) adder_1 (.a(in_1), .b(in_2), .out(adder_1_out), .cout(adder_1_cout));  // open: cin
  Subtractor #(.width(16)) subtractor_1 (
    .a(in_1), .b(in_2), .out(subtractor_1_out), .bout(subtractor_1_bout));  // open: bin
  Multiplier #(.width(16)) multiplier_1 (.a(in_1), .b(in_2), .out(multiplier_1_out), .cout(i2));  // open: cin
  Divider #(.width(16)) divider_1 (.a(in_1), .b(in_2), .out(divider_1_out), .rem(i3));  // open: upper
  assign and_1_out = in_1 & in_2;  // AND_Gate and_1, 16 bits wide
  assign or_1_out = in_1 | in_2;  // OR_Gate or_1, 16 bits wide
  assign xor_1_out = in_1 ^ in_2;  // XOR_Gate xor_1, 16 bits wide
  assign nand_1_out = ~(in_1 & in_2);  // NAND_Gate nand_1, 16 bits wide
  assign nor_1_out = ~(in_1 | in_2);  // NOR_Gate nor_1, 16 bits wide
  assign xnor_1_out = ~(in_1 ^ in_2);  // XNOR_Gate xnor_1, 16 bits wide
  Comparator #(.width(16)) comparator_1 (.a(in_1), .b(in_2), .lt(comparator_1_lt));  // open: gt, eq
  assign i0 = {{15{1'b0}}, adder_1_cout};  // Bit_Extender bit_extender_1
  assign i1 = {{15{1'b0}}, subtractor_1_bout};  // Bit_Extender bit_extender_2
  assign bit_extender_3_out = {{15{1'b0}}, comparator_1_lt};  // Bit_Extender bit_extender_3
  Multiplexer #(.select(4), .width(16)) multiplexer_1 (
    .in0(adder_1_out), .in1(subtractor_1_out), .in2(multiplier_1_out), .in3(divider_1_out), .in4(and_1_out),
    .in5(or_1_out), .in6(xor_1_out), .in7(nand_1_out), .in8(nor_1_out), .in9(xnor_1_out),
    .in10(bit_extender_3_out), .out(out_5), .sel(in_3));  // open: in11, in12, in13, in14, in15, en
  Comparator #(.width(16)) comparator_2 (.a({16{1'b0}}), .b(out_5), .eq(out_4));  // open: gt, lt
  Multiplexer #(.select(2), .width(16), .enable("false")) multiplexer_2 (
    .in0(i0), .in1(i1), .in2(i2), .in3(i3),
    .out(_16_31multiplier_remainder_overflow_in_adder_negative_in_subtractor), .sel(in_3[1:0]));
endmodule
