// Logisim project p0.circ as structural Verilog: 1 circuit, main circuit main
module main (
  input  in_1,
  input  in_2,
  input  in_3,
  input  in_4,
  input  in_5,
  input  in_6,
  input  in_7,
  input  in_8,
  input  in_9,
  input  in_10,
  input  in_11,
  input  in_12,
  input  in_13,
  input  in_14,
  input  in_15,
  input  in_16,
  input  in_17,
  input  in_18,
  output out_19,
  output out_20,
  output out_21,
  output out_22
);

  wire clock_1_out, clock_2_out, clock_3_out, clock_4_out;

  Clock clock_1 (.out(clock_1_out));
  Clock clock_2 (.out(clock_2_out));
  J_K_Flip_Flop j_k_ff_1 (
    .J(in_1), .clk(clock_1_out), .K(in_2), .Q(out_19), .preset(in_4), .en(in_6), .reset(in_8));  // open: Qn
  S_R_Flip_Flop s_r_ff_1 (
    .S(in_10), .clk(clock_2_out), .R(in_11), .Q(out_21), .preset(in_13), .reset(in_17), .en(in_15));  // open: Qn
  Clock clock_3 (.out(clock_3_out));
  Clock clock_4 (.out(clock_4_out));
  T_Flip_Flop t_ff_1 (.clk(clock_3_out), .T(in_3), .Q(out_20), .preset(in_5), .reset(in_9), .en(in_7));  // open: Qn
  D_Flip_Flop d_ff_1 (.clk(clock_4_out), .D(in_12), .Q(out_22), .preset(in_14), .en(in_16), .reset(in_18));  // open: Qn
endmodule
