// Logisim project p3.circ as structural Verilog: 1 circuit, main circuit main
module main (
  input  in_1,
  input  in_2,
  input  in_3,
  input  in_4,
  output out_5,
  output out_6,
  output out_7,
  output out_8,
  output out_9,
  output out_10,
  output out_11,
  output out_12,
  output out_13,
  output out_14
);

  wire clock_1_out, clock_2_out;

  Clock clock_1 (.out(clock_1_out));
  Hex_Digit_Display hex_digit_display_1 (.value({out_8, out_7, out_6, out_5}));  // open: dp
  Clock clock_2 (.out(clock_2_out));
  T_Flip_Flop t_ff_1 (.clk(clock_1_out), .T(in_1), .Q(out_5), .reset(in_2));  // open: Qn, preset, en
  T_Flip_Flop t_ff_2 (.clk(clock_2_out), .T(in_3), .Q(out_9), .reset(in_4));  // open: Qn, preset, en
  T_Flip_Flop t_ff_3 (.clk(out_5), .T(in_1), .Q(out_6), .reset(in_2));  // open: Qn, preset, en
  T_Flip_Flop t_ff_4 (.clk(out_9), .T(in_3), .Q(out_10), .reset(in_4));  // open: Qn, preset, en
  T_Flip_Flop t_ff_5 (.clk(out_6), .T(in_1), .Q(out_7), .reset(in_2));  // open: Qn, preset, en
  T_Flip_Flop t_ff_6 (.clk(out_10), .T(in_3), .Q(out_11), .reset(in_4));  // open: Qn, preset, en
  T_Flip_Flop t_ff_7 (.clk(out_7), .T(in_1), .Q(out_8), .reset(in_2));  // open: Qn, preset, en
  T_Flip_Flop t_ff_8 (.clk(out_11), .T(in_3), .Q(out_12), .reset(in_4));  // open: Qn, preset, en
  T_Flip_Flop t_ff_9 (.clk(out_12), .T(in_3), .Q(out_13), .reset(in_4));  // open: Qn, preset, en
  T_Flip_Flop t_ff_10 (.clk(out_13), .T(in_3), .Q(out_14), .reset(in_4));  // open: Qn, preset, en
endmodule
