// Logisim project p4.circ as structural Verilog: 2 circuits, main circuit main
module main (
  input  i7,
  input  i6,
  input  i5,
  input  i4,
  input  i3,
  input  i2,
  input  i1,
  input  i0,
  input  shr_in,
  input  [1:0] select,
  output q6,
  output q5,
  output q4,
  output q3,
  output q2,
  output q1,
  output q0,
  output q7
);

  wire clk_out, n4_bit_1_out_8;

  Clock clk (.out(clk_out));
  _4_bit u_4_bit_1 (
    .in_5(shr_in), .select(select), .clk(clk_out), .in_1(i7), .in_2(i6), .in_3(i5), .in_4(i4), .out_9(q7),
    .out_10(q6), .out_11(q5), .out_12(q4), .out_8(n4_bit_1_out_8));
  _4_bit u_4_bit_2 (
    .in_5(n4_bit_1_out_8), .select(select), .clk(clk_out), .in_1(i3), .in_2(i2), .in_3(i1), .in_4(i0),
    .out_9(q3), .out_10(q2), .out_11(q1), .out_12(q0));  // open: out_8
endmodule

module _4_bit (
  input  in_1,
  input  in_2,
  input  in_3,
  input  in_4,
  input  in_5,
  input  [1:0] select,
  input  clk,
  output out_8,
  output out_9,
  output out_10,
  output out_11,
  output out_12
);

  wire multiplexer_1_out, multiplexer_2_out, multiplexer_3_out, multiplexer_4_out;

  Multiplexer #(.select(2)) multiplexer_1 (
    .in0(out_9), .in1(in_1), .in2(in_5), .in3(1'b0), .out(multiplexer_1_out), .sel(select));  // open: en
  D_Flip_Flop d_ff_1 (.clk(clk), .D(multiplexer_1_out), .Q(out_9));  // open: Qn, preset, en, reset
  Multiplexer #(.select(2)) multiplexer_2 (
    .in0(out_10), .in1(in_2), .in2(out_9), .in3(1'b0), .out(multiplexer_2_out), .sel(select));  // open: en
  D_Flip_Flop d_ff_2 (.clk(clk), .D(multiplexer_2_out), .Q(out_10));  // open: Qn, preset, en, reset
  Multiplexer #(.select(2)) multiplexer_3 (
    .in0(out_11), .in1(in_3), .in2(out_10), .in3(1'b0), .out(multiplexer_3_out), .sel(select));  // open: en
  D_Flip_Flop d_ff_3 (.clk(clk), .D(multiplexer_3_out), .Q(out_11));  // open: Qn, preset, en, reset
  Multiplexer #(.select(2)) multiplexer_4 (
    .in0(out_8), .in1(in_4), .in2(out_11), .in3(1'b0), .out(multiplexer_4_out), .sel(select));  // open: en
  D_Flip_Flop d_ff_4 (.clk(clk), .D(multiplexer_4_out), .Q(out_8));  // open: Qn, preset, en, reset

  assign out_12 = out_8;
endmodule
