// Logisim project project.circ as structural Verilog: 4 circuits, main circuit main
module main (
  input  restart
);

  wire and_1_out, clock_1_out, clock_2_out, comparator_1_eq, L_out, multiplexer_1_out, multiplexer_2_out,
       not_1_out, R_out;
  wire [15:0] and_2_out, disp_1_out_3, disp_1_out_4, disp_1_out_5, disp_1_out_6, disp_1_out_7, disp_1_out_8,
       disp_1_out_9, disp_1_out_10, disp_1_out_11, disp_1_out_12, disp_1_out_13, disp_1_out_14,
       disp_1_out_15, disp_1_out_16, disp_1_out_17, disp_1_out_18, object_control_1_out_4, or_1_out,
       or_2_out, or_3_out;

  Clock #(.highDuration(2), .lowDuration(2)) clock_1 (.out(clock_1_out));
  and and_1 (and_1_out, clock_1_out, comparator_1_eq);
  Button L (.out(L_out));
  Clock clock_2 (.out(clock_2_out));
  Multiplexer multiplexer_1 (.in0(1'b0), .in1(1'b1), .out(multiplexer_1_out), .sel(L_out));  // open: en
  Button R (.out(R_out));
  Multiplexer multiplexer_2 (.in0(1'b0), .in1(1'b1), .out(multiplexer_2_out), .sel(R_out));  // open: en
  disp disp_1 (
    .clock(and_1_out), .reset(restart), .out_3(disp_1_out_3), .out_4(disp_1_out_4), .out_5(disp_1_out_5),
    .out_6(disp_1_out_6), .out_7(disp_1_out_7), .out_8(disp_1_out_8), .out_9(disp_1_out_9),
    .out_10(disp_1_out_10), .out_11(disp_1_out_11), .out_12(disp_1_out_12), .out_13(disp_1_out_13),
    .out_14(disp_1_out_14), .out_15(disp_1_out_15), .out_16(disp_1_out_16), .out_17(disp_1_out_17),
    .out_18(disp_1_out_18));
  Object_Control object_control_1 (
    .in_1(clock_2_out), .l(multiplexer_1_out), .r(multiplexer_2_out), .out_4(object_control_1_out_4));
  assign or_1_out = disp_1_out_16 | object_control_1_out_4;  // OR_Gate or_1, 16 bits wide
  assign or_2_out = disp_1_out_17 | object_control_1_out_4;  // OR_Gate or_2, 16 bits wide
  assign or_3_out = disp_1_out_18 | object_control_1_out_4;  // OR_Gate or_3, 16 bits wide
  DotMatrix #(.inputtype("row"), .matrixcols(16), .matrixrows(16)) dotmatrix_1 (
    .row0(disp_1_out_3), .row1(disp_1_out_4), .row2(disp_1_out_5), .row3(disp_1_out_6), .row4(disp_1_out_7),
    .row5(disp_1_out_8), .row6(disp_1_out_9), .row7(disp_1_out_10), .row8(disp_1_out_11),
    .row9(disp_1_out_12), .row10(disp_1_out_13), .row11(disp_1_out_14), .row12(disp_1_out_15),
    .row13(or_1_out), .row14(or_2_out), .row15(or_3_out));
  assign and_2_out = disp_1_out_16 & object_control_1_out_4;  // AND_Gate and_2, 16 bits wide
  Comparator #(.width(16)) comparator_1 (.a(and_2_out), .b({16{1'b0}}), .eq(comparator_1_eq));  // open: gt, lt
  not not_1 (not_1_out, comparator_1_eq);
  LED gameover (.in(not_1_out));
endmodule

module disp (
  input  clock,
  input  reset,
  output [15:0] out_3,
  output [15:0] out_4,
  output [15:0] out_5,
  output [15:0] out_6,
  output [15:0] out_7,
  output [15:0] out_8,
  output [15:0] out_9,
  output [15:0] out_10,
  output [15:0] out_11,
  output [15:0] out_12,
  output [15:0] out_13,
  output [15:0] out_14,
  output [15:0] out_15,
  output [15:0] out_16,
  output [15:0] out_17,
  output [15:0] out_18
);

  wire [15:0] inputselect_1_out_2;

  inputselect inputselect_1 (.clock(clock), .out_2(inputselect_1_out_2));
  Register #(.width(16)) register_1 (.D(inputselect_1_out_2), .Q(out_3), .clk(clock), .clr(reset));  // open: en
  Register #(.width(16)) register_2 (.D(out_3), .Q(out_4), .clk(clock), .clr(reset));  // open: en
  Register #(.width(16)) register_3 (.D(out_4), .Q(out_5), .clk(clock), .clr(reset));  // open: en
  Register #(.width(16)) register_4 (.D(out_5), .Q(out_6), .clk(clock), .clr(reset));  // open: en
  Register #(.width(16)) register_5 (.D(out_6), .Q(out_7), .clk(clock), .clr(reset));  // open: en
  Register #(.width(16)) register_6 (.D(out_7), .Q(out_8), .clk(clock), .clr(reset));  // open: en
  Register #(.width(16)) register_7 (.D(out_8), .Q(out_9), .clk(clock), .clr(reset));  // open: en
  Register #(.width(16)) register_8 (.D(out_9), .Q(out_10), .clk(clock), .clr(reset));  // open: en
  Register #(.width(16)) register_9 (.D(out_10), .Q(out_11), .clk(clock), .clr(reset));  // open: en
  Register #(.width(16)) register_10 (.D(out_11), .Q(out_12), .clk(clock), .clr(reset));  // open: en
  Register #(.width(16)) register_11 (.D(out_12), .Q(out_13), .clk(clock), .clr(reset));  // open: en
  Register #(.width(16)) register_12 (.D(out_13), .Q(out_14), .clk(clock), .clr(reset));  // open: en
  Register #(.width(16)) register_13 (.D(out_14), .Q(out_15), .clk(clock), .clr(reset));  // open: en
  Register #(.width(16)) register_14 (.D(out_15), .Q(out_16), .clk(clock), .clr(reset));  // open: en
  Register #(.width(16)) register_15 (.D(out_16), .Q(out_17), .clk(clock), .clr(reset));  // open: en
  Register #(.width(16)) register_16 (.D(out_17), .Q(out_18), .clk(clock), .clr(reset));  // open: en
endmodule

module inputselect (
  input  clock,
  output [15:0] out_2
);

  wire and_1_out, s0_qn, xor_1_out, xor_2_out;
  wire [2:0] random_1_out, s0_q;
  wire [15:0] multiplexer_1_out;

  D_Flip_Flop s0 (.clk(clock), .D(s0_qn), .Q(s0_q[0]), .Qn(s0_qn));  // open: preset, en, reset
  xor xor_1 (xor_1_out, s0_q[1], s0_q[0]);
  and and_1 (and_1_out, s0_q[0], s0_q[1]);
  D_Flip_Flop s1 (.clk(clock), .D(xor_1_out), .Q(s0_q[1]));  // open: Qn, preset, en, reset
  xor xor_2 (xor_2_out, and_1_out, s0_q[2]);
  D_Flip_Flop s2 (.clk(clock), .D(xor_2_out), .Q(s0_q[2]));  // open: Qn, preset, en, reset
  Multiplexer #(.select(3), .width(16)) multiplexer_1 (
    .in0(16'h6), .in1(16'h6), .in2(16'h60), .in3(16'h600), .in4(16'h6000), .in5(16'h6060), .in6(16'h6006),
    .in7(16'h606), .out(multiplexer_1_out), .sel(random_1_out));  // open: en
  Random #(.width(3), .trigger("falling")) random_1 (.clk(s0_q[2]), .out(random_1_out));  // open: next, clr
  Multiplexer #(.width(16)) multiplexer_2 (
    .in0(multiplexer_1_out), .in1({16{1'b0}}), .out(out_2), .sel(s0_q[2]));  // open: en
  Hex_Digit_Display hex_digit_display_1 (.value({1'b0, s0_q}));  // open: dp
endmodule

module Object_Control (
  input  in_1,
  input  l,
  input  r,
  output [15:0] out_4
);

  wire and_1_out, and_2_out, and_3_out, and_4_out, and_5_out, and_6_out, and_7_out, clock_1_out, not_1_out,
       not_2_out, or_1_out, or_2_out, s0_qn;
  wire [1:0] s0_q;

  not not_1 (not_1_out, l);
  Clock clock_1 (.out(clock_1_out));
  not not_2 (not_2_out, r);
  D_Flip_Flop s1 (.clk(clock_1_out), .D(or_1_out), .Q(s0_q[1]));  // open: Qn, preset, en, reset
  D_Flip_Flop s0 (.clk(clock_1_out), .D(or_2_out), .Q(s0_q[0]), .Qn(s0_qn));  // open: preset, en, reset
  and and_1 (and_1_out, s0_q[0], r);
  and and_2 (and_2_out, s0_q[1], not_1_out);
  and and_3 (and_3_out, s0_q[1], s0_q[0]);
  and and_4 (and_4_out, s0_qn, r);
  and and_5 (and_5_out, s0_q[1], r);
  and and_6 (and_6_out, not_1_out, s0_q[0], not_2_out);
  and and_7 (and_7_out, s0_q[1], s0_qn, l);
  or or_1 (or_1_out, and_1_out, and_2_out, and_3_out);
  or or_2 (or_2_out, and_4_out, and_5_out, and_6_out, and_7_out);
  Multiplexer #(.select(2), .width(16)) multiplexer_1 (
    .in0(16'h6000), .in1(16'h600), .in2(16'h60), .in3(16'h6), .out(out_4), .sel(s0_q));  // open: en
endmodule
