// Logisim project Simple_router.circ as structural Verilog: 1 circuit, main circuit main
module main (
  input  [24:0] in_1,
  input  in_2,
  output Port1enable,
  output [24:0] output_port1,
  output Port2enable,
  output [24:0] output_port2
);

  wire Add____128, and_1_out, and_2_out, and_3_out, and_4_out, and_5_out, and_6_out, clock_1_out,
       CS____Pkt_24__16, not_1_out, not_2_out, not_3_out, or_1_out, or_2_out, s0, s1, s2;
  wire [7:0] adder_1_out;
  wire [8:0] register_2_q;
  wire [8:8] adder_1_cout;
  wire [24:0] register_1_q;

  not not_1 (not_1_out, s2);
  not not_2 (not_2_out, s1);
  Register #(.width(25)) register_1 (.D(in_1), .en(in_2), .Q(register_1_q), .clk(clock_1_out));  // open: clr
  not not_3 (not_3_out, s0);
  Adder adder_1 (.a(in_1[7:0]), .b(in_1[15:8]), .out(adder_1_out), .cout(adder_1_cout[8]));  // open: cin
  and and_1 (and_1_out, not_1_out, s1, s0);
  and and_2 (and_2_out, not_1_out, not_2_out, s0);
  and and_3 (and_3_out, not_1_out, s1, not_3_out, CS____Pkt_24__16);
  and and_4 (and_4_out, in_2, not_1_out, not_2_out, not_3_out);
  and and_5 (and_5_out, not_1_out, s1, not_3_out, CS____Pkt_24__16);
  and and_6 (and_6_out, not_1_out, s1, s0, Add____128);
  and and_7 (Port1enable, s2, not_2_out, not_3_out);
  and and_8 (Port2enable, s2, not_2_out, s0);
  Register #(.width(9)) register_2 (
    .D({adder_1_cout[8], adder_1_out}), .en(in_2), .Q(register_2_q), .clk(clock_1_out));  // open: clr
  or or_1 (or_1_out, and_2_out, and_3_out);
  or or_2 (or_2_out, and_4_out, and_5_out, and_6_out);
  Comparator #(.width(9)) comparator_1 (
    .a(register_1_q[24:16]), .b(register_2_q), .eq(CS____Pkt_24__16));  // open: gt, lt
  Register #(.width(1)) D2 (.D(and_1_out), .Q(s2), .clk(clock_1_out));  // open: en, clr
  Comparator #(.mode("unsigned")) comparator_2 (.a(register_1_q[7:0]), .b(8'h7f), .gt(Add____128));  // open: eq, lt
  Register #(.width(1)) D1 (.D(or_1_out), .Q(s1), .clk(clock_1_out));  // open: en, clr
  Multiplexer #(.width(25)) multiplexer_1 (.in1(register_1_q), .out(output_port1), .sel(Port1enable));  // open: in0, en
  Multiplexer #(.width(25)) multiplexer_2 (.in1(register_1_q), .out(output_port2), .sel(Port2enable));  // open: in0, en
  Register #(.width(1)) D0 (.D(or_2_out), .Q(s0), .clk(clock_1_out));  // open: en, clr
  Clock clock_1 (.out(clock_1_out));
endmodule
